# Fritzing sketch dispenser (saved by Fritzing 0.9.3b)

parts:
  ZS-042_RTC1 = ZS-042 RTC Module
  Squix1 = OLED 0.91" 128x32 I2C SSD1306 (GND/VCC)
  M1 = DC Motor
  U1 = L9110 H-bridge module [part_number="L9110 H-bridge"]
  D2F1 = D2F-FL Omron Snap Action Limit Switch with Level
  D2F2 = D2F-FL Omron Snap Action Limit Switch with Level
  R2 = Resistor [tolerance=±5% resistance=220 package="2010 [SMD]"]
  Componente1 = Arduino Uno (Rev3) - ICSP
  R1 = Resistor [tolerance=±5% resistance=220 package="2010 [SMD]"]
  kEYPAD_MATRICIAL_1 = KEYPAD_4x3

nets:
  N1: ZS-042_RTC1.GND#0, R2.Pin_0, Componente1.GND
  N2: ZS-042_RTC1.VCC#1, Componente1.5V
  N3: ZS-042_RTC1.SDA#2, Componente1.A4/SDA
  N4: ZS-042_RTC1.SCL#3, Componente1.A5/SCL
  N5: ZS-042_RTC1.GND#6, Squix1.GND
  N6: ZS-042_RTC1.VCC#7, Squix1.VCC
  N7: ZS-042_RTC1.SDA#8, Squix1.SCA
  N8: ZS-042_RTC1.SCL#9, Squix1.SCL
  N9: M1.pin_1, U1.MOTOR_A-B
  N10: M1.pin_2, U1.MOTOR_A-A
  N11: U1.A-IA, Componente1.A3, R1.Pin_1
  N12: U1.A-IB, R2.Pin_1, Componente1.A2
  N13: D2F1.COM, Componente1.A1
  N14: D2F2.COM, Componente1.A0
  N15: Componente1.D8, kEYPAD_MATRICIAL_1.connector29
  N16: Componente1.D9_PWM, kEYPAD_MATRICIAL_1.connector30
  N17: Componente1.D10_PWM/SS, kEYPAD_MATRICIAL_1.connector31
  N18: Componente1.D4, kEYPAD_MATRICIAL_1.connector25
  N19: Componente1.D5_PWM, kEYPAD_MATRICIAL_1.connector26
  N20: Componente1.D6_PWM, kEYPAD_MATRICIAL_1.connector27
  N21: Componente1.D7, kEYPAD_MATRICIAL_1.connector28

custom parts:
  OLED 0.91" 128x32 I2C SSD1306 (GND/VCC): OLED 0.91" 128x32 I2C SSD1306 Pinout: GND/VCC/SCL/SDA
  D2F-FL Omron Snap Action Limit Switch with Level: Snap action switch with stainless steel lever.
